# Fritzing sketch macao (saved by Fritzing 0.7.4b)
breadboards: 1

parts:
  R1 = Resistor [tolerance=±5% resistance=4.7k package=THT]
  Q1 = NPN-Transistor [part_number=BC337 package="TO92 [THT]"]
  Arduino1 = Arduino
  D1 = Rectifier Diode [part_number=1N4001 package="300 mil [THT]"]
  J1 = Screw terminal - 2 pins [package=THT]
  K1 = Relay [part_number=FRS1B-S package=THT]
  R2 = Resistor [tolerance=±5% resistance=4.7k package=THT]
  Q2 = NPN-Transistor [part_number=BC337 package="TO92 [THT]"]
  D2 = Rectifier Diode [part_number=1N4001 package="300 mil [THT]"]
  J2 = Screw terminal - 2 pins [package=THT]
  K2 = Relay [part_number=FRS1B-S package=THT]

nets:
  N1: R1.Pin_0, Q1.B
  N2: R1.Pin_1, Arduino1.D13
  GND: Q1.E, Q2.E
  N3: Q1.C, D1.anode, K1.COIL1
  N4: Arduino1.D12, R2.Pin_1
  12V: D1.cathode, K1.COIL2, D2.cathode, K2.COIL2
  N5: J1.pin1, K1.B
  N6: J1.pin2, K1.C2
  N7: R2.Pin_0, Q2.B
  N8: Q2.C, D2.anode, K2.COIL1
  N9: J2.pin1, K2.B
  N10: J2.pin2, K2.C2
